// Logisim project KeyFinder_Sim.circ as structural Verilog: 1 circuit, main circuit main
module main (
);

  wire buffer_1_out, clock_1_out, d_ff_1_q, d_ff_1_qn, pull_resistor_1_node;

  Clock #(.highDuration(5), .lowDuration(10)) clock_1 (.out(clock_1_out));
  buf buffer_1 (buffer_1_out, clock_1_out);
  Pull_Resistor #(.pull(1)) pull_resistor_1 (.node(pull_resistor_1_node));
  // Probe on d_ff_1_q
  // Probe on d_ff_1_qn
  D_Flip_Flop #(.trigger("high")) d_ff_1 (
    .clk(pull_resistor_1_node), .D(buffer_1_out), .Q(d_ff_1_q), .Qn(d_ff_1_qn));  // open: preset, en, reset
endmodule
